# Fritzing sketch Breadboard1 (saved by Fritzing 0.9.3b)
breadboards: 2

parts:
  R1 = Resistor [tolerance=±5% resistance=100k package="0603 [SMD]"]
  Input_Gain = Trimmer Potentiometer [maximum_resistance=100k package=THT]
  R4 = Resistor [tolerance=±5% resistance=4.7k package="0603 [SMD]"]
  C9 = Ceramic Capacitor [capacitance=10nF voltage=50V part_number=6n8 package="0603 [SMD, multilayer]"]
  C10 = Ceramic Capacitor [capacitance=10pF voltage=50V part_number=270pF package="0603 [SMD, multilayer]"]
  R5 = Resistor [tolerance=±5% resistance=4.7k package="0603 [SMD]"]
  C11 = Ceramic Capacitor [capacitance=10nF voltage=50V part_number=6n8 package="0603 [SMD, multilayer]"]
  R6 = Resistor [tolerance=±5% resistance=1M package="0603 [SMD]"]
  R13 = Resistor [tolerance=±5% resistance=4.7k part_number=4k7 package="0603 [SMD]"]
  Raise/Lower = Pushbutton [package="[THT]"]
  S2 = Pushbutton [package="[THT]"]
  C20 = Ceramic Capacitor [capacitance=100nF voltage=50V part_number=0.1uF package="0603 [SMD, multilayer]"]
  C21 = Ceramic Capacitor [capacitance=100nF voltage=50V part_number=0.1uF package="0603 [SMD, multilayer]"]
  Input = AMPHENOL - ACJS-MHDR [package=ACJS-MHDR]
  C22 = Ceramic Capacitor [capacitance=100nF voltage=50V part_number=0.1uF package="0603 [SMD, multilayer]"]
  Output = AMPHENOL - ACJS-MHDR [package=ACJS-MHDR]
  TLC2272 = Dual Op-Amp [package=dip08]
  C23 = Electrolytic Capacitor [capacitance=47µF voltage=16V package="1010 [SMD, electrolytic]"]
  C24 = Electrolytic Capacitor [capacitance=47µF voltage=16V package="1010 [SMD, electrolytic]"]
  C25 = Electrolytic Capacitor [capacitance=10µF voltage=16V package="1010 [SMD, electrolytic]"]
  Effects = Pushbutton [package="[THT]"]
  Effect_On = LED - 3mm [color="Red (633nm)" package="3 mm [THT]"]
  R18 = Resistor [tolerance=±5% resistance=470 package="0603 [SMD]"]
  R19 = Resistor [tolerance=±5% resistance=4.7k package="0603 [SMD]"]
  R14 = Resistor [tolerance=±5% resistance=1M part_number=1M2 package=THT]
  Atmega1284 = ATmega644 [package=pdpi]
  Y1 = CRYSTAL [package=hc49u-v]
  C26 = Ceramic Capacitor [capacitance=10pF voltage=50V part_number=22pF package="0603 [SMD, multilayer]"]
  C27 = Ceramic Capacitor [capacitance=10pF voltage=50V part_number=27pF package="0603 [SMD, multilayer]"]
  C30 = Ceramic Capacitor [capacitance=100nF voltage=50V part_number=100nF package="0603 [SMD, multilayer]"]
  C31 = Ceramic Capacitor [capacitance=100nF voltage=50V part_number=0.1uF package="0603 [SMD, multilayer]"]
  Power_5v = Power plug
  C32 = Ceramic Capacitor [capacitance=100nF voltage=50V part_number=0.1uF package="0603 [SMD, multilayer]"]
  R20 = Resistor [tolerance=±5% resistance=4.7k package="0603 [SMD]"]
  C33 = Ceramic Capacitor [capacitance=10nF voltage=50V part_number=6n8 package="0603 [SMD, multilayer]"]
  R21 = Resistor [tolerance=±5% resistance=4.7k package="0603 [SMD]"]
  C34 = Ceramic Capacitor [capacitance=10nF voltage=50V part_number=6n8 package="0603 [SMD, multilayer]"]
  R22 = Resistor [tolerance=±5% resistance=1M package="0603 [SMD]"]
  part = Ceramic Capacitor [capacitance=100nF package="100 mil [THT, multilayer]"]

nets:
  N1: R1.Pin_0, C10.0, TLC2272.B_OUT, R19.Pin_1
  N2: R1.Pin_1, Input_Gain.leg1, Input_Gain.wiper, C10.1, TLC2272.B_-IN
  N3: Input_Gain.leg2, R4.Pin_1
  N4: R4.Pin_0, C25.+
  N5: C9.0, C11.0, R6.Pin_0, C21.0, Input.Sleeve_(4), C23.-, C25.-, Effect_On.cathode
  N6: C9.1, R19.Pin_0, Atmega1284.PA0
  N7: R5.Pin_0, C11.1, TLC2272.B_+IN
  N8: R5.Pin_1, R6.Pin_1, C22.1, R22.Pin_1
  N9: R13.Pin_0, Atmega1284.PD4
  N10: R13.Pin_1, R14.Pin_1, R21.Pin_0, C34.1
  GND: Raise/Lower.Pin_1, Raise/Lower.Pin_2, S2.Pin_1, S2.Pin_2, C20.0, Output.Sleeve_(1), TLC2272.A_V-, C24.-, Effects.Pin_1, Effects.Pin_2, Atmega1284.GND, C26.1, C27.0, C30.1, C31.0, Power_5v.GND, C32.0, C34.0
  N11: Raise/Lower.Pin_3, Raise/Lower.Pin_4, Atmega1284.PA4
  N12: S2.Pin_3, S2.Pin_4, Atmega1284.PA5
  VCC: C20.1, C24.+, Atmega1284.VCC, Atmega1284.AVCC, C31.1, Power_5v.VCC, C32.1
  N13: C21.1, TLC2272.A_V+, C23.+, R22.Pin_0
  N14: Input.Tip_(6), C22.0
  N15: Output.Tip_(3), part.1
  N16: TLC2272.A_OUT, TLC2272.A_-IN, C33.1, part.0
  N17: TLC2272.A_+IN, R20.Pin_0
  N18: Effects.Pin_3, Effects.Pin_4, Atmega1284.PB1
  N19: Effect_On.anode, R18.Pin_0
  N20: R18.Pin_1, Atmega1284.PB0
  N21: R14.Pin_0, Atmega1284.PD5
  N22: Atmega1284.XTAL2, Y1.1, C27.1
  N23: Atmega1284.XTAL1, Y1.2, C26.0
  N24: Atmega1284.AREF, C30.0
  N25: R20.Pin_1, C33.0, R21.Pin_1
